// Logisim project decoder_from_image.circ as structural Verilog: 1 circuit, main circuit main
module main (
  input  A0,
  input  A1,
  output D0,
  output D1,
  output D2,
  output D3
);

  wire not_1_out, not_2_out, undriven, undriven_2;

  not not_1 (not_1_out, A0);
  not not_2 (not_2_out, A1);
  and and_1 (D0, not_1_out, not_2_out);
  and and_2 (D1, undriven, not_2_out);
  and and_3 (D2, not_1_out, undriven_2);
  and and_4 (D3, A0, A1);
endmodule
